// Digital circuit front.dig as structural Verilog
module front (
  input  [15:0] value,
  input  [1:0] dest,
  input  [1:0] src,
  output [15:0] R0,
  output [15:0] R1,
  output [15:0] R2,
  output [15:0] R3,
  output [15:0] B,
  output [1:0] rs,
  output [15:0] A,
  output [15:0] B_2,
  output [1:0] rd
);

  wire add_out, asm_1_store_clk, button_1_out, jmp_out, mode_out;
  wire [1:0] PC_out;
  wire [15:0] execute_1_sum;
  wire [31:0] asm_1_inst, Program_d;

  LED programming (.in(mode_out));
  DipSwitch mode (.out(mode_out));
  Button add (.out(add_out));
  Button jmp (.out(jmp_out));
  asm asm_1 (
    .mode(mode_out), .imm(value), .dest(dest), .src(src), .add(add_out), .jump(jmp_out), .inst(asm_1_inst),
    .store_clk(asm_1_store_clk));
  EEPROMDualPort #(.Bits(32)) Program (
    .A(PC_out), .Din(asm_1_inst), .str(1'b1), .C(asm_1_store_clk), .ld(1'b1), .D(Program_d));
  Counter #(.Bits(2)) PC (.en(1'b1), .C(button_1_out), .clr(1'b0), .out(PC_out));  // open: ovf
  Button button_1 (.out(button_1_out));
  // decoder decoder_1: pin names not known; wires that end beside it: mode_out, Program_d, asm_1_inst, A, rs, rd
  execute execute_1 (.A(A), .B(B), .sum(execute_1_sum));
  regfile regfile_1 (.rs(rs), .rd(rd), .D(execute_1_sum), .CL(button_1_out), .R0(B), .R1(R0), .R2(R1), .R3(R2), .B(R3));

  assign B_2 = B;

  // Notes on the sheet:
  //   contents of Program (hex, n*v repeats v):
  //   10064,1200c8,230063,300022
endmodule
